// Logisim project 1.circ as structural Verilog: 1 circuit, main circuit main
module main (
  input  [3:0] in_1,
  input  [3:0] in_2,
  input  [3:0] in_3,
  input  [3:0] in_4,
  input  [3:0] in_5,
  input  [3:0] in_6,
  input  [3:0] in_7,
  input  [3:0] in_8,
  output out_9
);

  wire clock_1_out, comparator_1_eq, comparator_2_eq, comparator_3_eq, comparator_4_eq, comparator_5_eq,
       comparator_6_eq, comparator_7_eq, comparator_8_eq;
  wire [3:0] register_1_q, register_2_q, register_3_q, register_4_q, register_5_q, register_6_q,
       register_7_q, register_8_q;

  Clock clock_1 (.out(clock_1_out));
  Register #(.width(4)) register_1 (.D(in_1), .Q(register_1_q), .clk(clock_1_out));  // open: en, clr
  Register #(.width(4)) register_2 (.D(in_2), .Q(register_2_q), .clk(clock_1_out));  // open: en, clr
  Register #(.width(4)) register_3 (.D(in_3), .Q(register_3_q), .clk(clock_1_out));  // open: en, clr
  Register #(.width(4)) register_4 (.D(in_4), .Q(register_4_q), .clk(clock_1_out));  // open: en, clr
  Register #(.width(4)) register_5 (.D(in_5), .Q(register_5_q), .clk(clock_1_out));  // open: en, clr
  Register #(.width(4)) register_6 (.D(in_6), .Q(register_6_q), .clk(clock_1_out));  // open: en, clr
  Register #(.width(4)) register_7 (.D(in_7), .Q(register_7_q), .clk(clock_1_out));  // open: en, clr
  Register #(.width(4)) register_8 (.D(in_8), .Q(register_8_q), .clk(clock_1_out));  // open: en, clr
  and and_1 (out_9, comparator_8_eq, comparator_7_eq, comparator_6_eq, comparator_4_eq, comparator_3_eq, comparator_2_eq, comparator_1_eq);
  Comparator #(.width(4)) comparator_1 (.a(register_1_q), .b(4'b0001), .eq(comparator_1_eq));  // open: gt, lt
  Comparator #(.width(4)) comparator_2 (.a(register_2_q), .b(4'b1001), .eq(comparator_2_eq));  // open: gt, lt
  Comparator #(.width(4)) comparator_3 (.a(register_3_q), .b(4'b0101), .eq(comparator_3_eq));  // open: gt, lt
  Comparator #(.width(4)) comparator_4 (.a(register_4_q), .b(4'b0010), .eq(comparator_4_eq));  // open: gt, lt
  Comparator #(.width(4)) comparator_5 (.a(register_5_q), .b(4'b0000), .eq(comparator_5_eq));  // open: gt, lt
  Comparator #(.width(4)) comparator_6 (.a(register_6_q), .b(4'b0011), .eq(comparator_6_eq));  // open: gt, lt
  Comparator #(.width(4)) comparator_7 (.a(register_7_q), .b(4'b0100), .eq(comparator_7_eq));  // open: gt, lt
  Comparator #(.width(4)) comparator_8 (.a(register_8_q), .b(4'b0101), .eq(comparator_8_eq));  // open: gt, lt
endmodule
